# Fritzing sketch wiring_music_maker (saved by Fritzing 0.9.3b)

parts:
  U1 = NodeMCU V3.0
  RFID_Reader = RFID-RC522-v2
  SP1 = SPEAKER [package=pcb_mount_speaker]
  Adafruit_Music_Maker_FeatherWing = Adafruit Music Maker FeatherWing with Amp [part_number="Adafruit #3436"]

nets:
  N1: U1.D0, Adafruit_Music_Maker_FeatherWing.XDCS
  N2: U1.D1, Adafruit_Music_Maker_FeatherWing.DREQ
  N3: U1.D2, Adafruit_Music_Maker_FeatherWing.SD_CS
  N4: U1.D3, Adafruit_Music_Maker_FeatherWing.MP3CS
  GND: U1.GND, RFID_Reader.GND, Adafruit_Music_Maker_FeatherWing.GND
  N5: U1.D5, RFID_Reader.SCK, Adafruit_Music_Maker_FeatherWing.SCLK
  N6: U1.D6, RFID_Reader.MISO, Adafruit_Music_Maker_FeatherWing.MISO
  N7: U1.D7, RFID_Reader.MOSI, Adafruit_Music_Maker_FeatherWing.MOSI
  N8: U1.D8, RFID_Reader.SDA
  3.3V: U1.3V3, RFID_Reader.3.3V, Adafruit_Music_Maker_FeatherWing.3.3V
  N9: U1.Vin, Adafruit_Music_Maker_FeatherWing.USB
  N10: SP1.+, Adafruit_Music_Maker_FeatherWing.OUT_RIGHT+
  N11: SP1.-, Adafruit_Music_Maker_FeatherWing.OUT_RIGHT-

custom parts:
  NodeMCU V3.0: ESP8266 based NodeMCU
  RFID-RC522-v2: A simple China made RFID-RC522 Reader; do check the pin labels, as this is a MFRC522 based clone.
  Adafruit Music Maker FeatherWing with Amp: Bend all audio files to your will with the Adafruit Music Maker FeatherWing + Amplifier! It's a fun-size version of our Music Maker shield for Arduino, and similar to our other Music Maker FeatherWing, but this one is even better - with an on-board 3 Watt amplifier! This powerful wing features the VS1053, an encoding/decoding (codec) chip that can decode a wide variety of audio formats such as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
